# Fritzing sketch X10Controller (saved by Fritzing 1.0.1rc)

parts:
  DB9 = DB9 Connector [package=db9]
  OLED = Grove OLED 128x96
  Feather_Huzzah = Adafruit Feather HUZZAH ESP8266 [part_number="Adafruit #2821"]

nets:
  N1: DB9.4, Feather_Huzzah.GPIO12/MISO
  GND: DB9.5, OLED.GND, Feather_Huzzah.GND
  N2: DB9.7, Feather_Huzzah.GPIO14/SCK
  VCC: OLED.VCC, Feather_Huzzah.3.3V
  N3: OLED.SDA, Feather_Huzzah.GPIO4/SDA
  N4: OLED.SCL, Feather_Huzzah.GPIO5/SCL

custom parts:
  Adafruit Feather HUZZAH ESP8266: his is the Adafruit Feather HUZZAH ESP8266 - our take on an 'all-in-one' ESP8266 WiFi development board with built in USB and battery charging. Its an ESP8266 WiFi module with all the extras you need, ready to rock! We have other boards in the Feather family, check'em out here. At the Feather HUZZAH's heart is an ESP8266 WiFi microcontroller clocked at 80 MHz and at 3.3V logic. This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
